// Logisim project 2-way associative - continue.circ as structural Verilog: 2 circuits, main circuit main
module main (
  input  [31:0] in_1
);

  wire and_1_out, and_2_out, not_1_out, or_1_out;
  wire [27:0] ram_1_data, ram_2_data, xnor_1_out, xnor_2_out;
  wire [31:0] ram_3_data;

  // Probe on ram_3_data
  RAM #(.addrWidth(2), .dataWidth(28)) ram_1 (.addr(in_1[3:2]), .data(ram_1_data));  // open: sel, clk, ld, clr
  RAM #(.addrWidth(2), .dataWidth(28)) ram_2 (.addr(in_1[3:2]), .data(ram_2_data));  // open: sel, clk, ld, clr
  RAM #(.addrWidth(2), .dataWidth(32)) ram_3 (
    .addr(in_1[3:2]), .data(ram_3_data), .sel(not_1_out));  // open: clk, ld, clr
  assign xnor_1_out = ~(ram_1_data ^ in_1[31:4]);  // XNOR_Gate xnor_1, 28 bits wide
  assign xnor_2_out = ~(in_1[31:4] ^ ram_2_data);  // XNOR_Gate xnor_2, 28 bits wide
  LED led_1 (.in(not_1_out));
  not not_1 (not_1_out, or_1_out);
  and and_1 (and_1_out, xnor_1_out[0], xnor_1_out[1], xnor_1_out[2], xnor_1_out[3], xnor_1_out[4], xnor_1_out[5], xnor_1_out[6], xnor_1_out[7], xnor_1_out[8], xnor_1_out[9], xnor_1_out[10], xnor_1_out[11], xnor_1_out[12], xnor_1_out[13], xnor_1_out[14], xnor_1_out[15], xnor_1_out[16], xnor_1_out[17], xnor_1_out[18], xnor_1_out[19], xnor_1_out[20], xnor_1_out[21], xnor_1_out[22], xnor_1_out[23], xnor_1_out[24], xnor_1_out[25], xnor_1_out[26], xnor_1_out[27]);
  and and_2 (and_2_out, xnor_2_out[0], xnor_2_out[1], xnor_2_out[2], xnor_2_out[3], xnor_2_out[4], xnor_2_out[5], xnor_2_out[6], xnor_2_out[7], xnor_2_out[8], xnor_2_out[9], xnor_2_out[10], xnor_2_out[11], xnor_2_out[12], xnor_2_out[13], xnor_2_out[14], xnor_2_out[15], xnor_2_out[16], xnor_2_out[17], xnor_2_out[18], xnor_2_out[19], xnor_2_out[20], xnor_2_out[21], xnor_2_out[22], xnor_2_out[23], xnor_2_out[24], xnor_2_out[25], xnor_2_out[26], xnor_2_out[27]);
  LED led_2 (.in(or_1_out));
  or or_1 (or_1_out, and_1_out, and_2_out);

  // Notes on the sheet:
  //   CPU
  //   BİNARY ADDRESS
  //   SET 1
  //   SET 2
  //   MAİN MEMORY
endmodule

module comparater (
  input  [27:0] in_1,
  input  [27:0] in_2,
  output out_3
);

  wire [27:0] xnor_1_out;

  assign xnor_1_out = ~(in_1 ^ in_2);  // XNOR_Gate xnor_1, 28 bits wide
  and and_1 (out_3, xnor_1_out[0], xnor_1_out[1], xnor_1_out[2], xnor_1_out[3], xnor_1_out[4], xnor_1_out[5], xnor_1_out[6], xnor_1_out[7], xnor_1_out[8], xnor_1_out[9], xnor_1_out[10], xnor_1_out[11], xnor_1_out[12], xnor_1_out[13], xnor_1_out[14], xnor_1_out[15], xnor_1_out[16], xnor_1_out[17], xnor_1_out[18], xnor_1_out[19], xnor_1_out[20], xnor_1_out[21], xnor_1_out[22], xnor_1_out[23], xnor_1_out[24], xnor_1_out[25], xnor_1_out[26], xnor_1_out[27]);
endmodule
