// Logisim project Direct Mapping.circ as structural Verilog: 2 circuits, main circuit main
module main (
  input  [31:0] in_1
);

  wire and_1_out, not_1_out;
  wire [27:0] ram_1_data, xnor_1_out;
  wire [31:0] ram_2_data;

  RAM #(.addrWidth(2), .dataWidth(28)) ram_1 (.addr(in_1[3:2]), .data(ram_1_data), .sel(1'b1));  // open: clk, ld, clr
  assign xnor_1_out = ~(ram_1_data ^ in_1[31:4]);  // XNOR_Gate xnor_1, 28 bits wide
  // Probe on ram_2_data
  RAM #(.addrWidth(2), .dataWidth(32)) ram_2 (
    .addr(in_1[3:2]), .data(ram_2_data), .sel(not_1_out));  // open: clk, ld, clr
  and and_1 (and_1_out, xnor_1_out[0], xnor_1_out[1], xnor_1_out[2], xnor_1_out[3], xnor_1_out[4], xnor_1_out[5], xnor_1_out[6], xnor_1_out[7], xnor_1_out[8], xnor_1_out[9], xnor_1_out[10], xnor_1_out[11], xnor_1_out[12], xnor_1_out[13], xnor_1_out[14], xnor_1_out[15], xnor_1_out[16], xnor_1_out[17], xnor_1_out[18], xnor_1_out[19], xnor_1_out[20], xnor_1_out[21], xnor_1_out[22], xnor_1_out[23], xnor_1_out[24], xnor_1_out[25], xnor_1_out[26], xnor_1_out[27]);
  LED led_1 (.in(not_1_out));
  not not_1 (not_1_out, and_1_out);
  LED led_2 (.in(and_1_out));
endmodule

module my_comparator (
  input  [27:0] in_1,
  input  [27:0] in_2,
  output out_3
);

  wire [27:0] xnor_1_out;

  assign xnor_1_out = ~(in_1 ^ in_2);  // XNOR_Gate xnor_1, 28 bits wide
  and and_1 (out_3, xnor_1_out[0], xnor_1_out[1], xnor_1_out[2], xnor_1_out[3], xnor_1_out[4], xnor_1_out[5], xnor_1_out[6], xnor_1_out[7], xnor_1_out[8], xnor_1_out[9], xnor_1_out[10], xnor_1_out[11], xnor_1_out[12], xnor_1_out[13], xnor_1_out[14], xnor_1_out[15], xnor_1_out[16], xnor_1_out[17], xnor_1_out[18], xnor_1_out[19], xnor_1_out[20], xnor_1_out[21], xnor_1_out[22], xnor_1_out[23], xnor_1_out[24], xnor_1_out[25], xnor_1_out[26], xnor_1_out[27]);
endmodule
