// Logisim project Full-associative.circ as structural Verilog: 2 circuits, main circuit main
module main (
  input  [31:0] in_1
);

  wire and_1_out, and_2_out, and_3_out, and_4_out, not_1_out, or_1_out;
  wire [29:0] ram_1_data, ram_2_data, ram_3_data, ram_4_data, ram_5_data, xnor_1_out, xnor_2_out, xnor_3_out,
       xnor_4_out;

  RAM #(.addrWidth(2), .dataWidth(30)) ram_1 (.addr(2'b11), .data(ram_1_data), .sel(1'b1));  // open: clk, ld, clr
  RAM #(.addrWidth(2), .dataWidth(30)) ram_2 (.addr(2'b11), .data(ram_2_data), .sel(1'b1));  // open: clk, ld, clr
  RAM #(.addrWidth(2), .dataWidth(30)) ram_3 (.addr(2'b11), .data(ram_3_data), .sel(1'b1));  // open: clk, ld, clr
  RAM #(.addrWidth(2), .dataWidth(30)) ram_4 (.addr(2'b11), .data(ram_4_data), .sel(1'b1));  // open: clk, ld, clr
  assign xnor_1_out = ~(ram_1_data ^ in_1[31:2]);  // XNOR_Gate xnor_1, 30 bits wide
  assign xnor_2_out = ~(ram_3_data ^ in_1[31:2]);  // XNOR_Gate xnor_2, 30 bits wide
  assign xnor_3_out = ~(ram_2_data ^ in_1[31:2]);  // XNOR_Gate xnor_3, 30 bits wide
  assign xnor_4_out = ~(ram_4_data ^ in_1[31:2]);  // XNOR_Gate xnor_4, 30 bits wide
  and and_1 (and_1_out, xnor_1_out[0], xnor_1_out[1], xnor_1_out[2], xnor_1_out[3], xnor_1_out[4], xnor_1_out[5], xnor_1_out[6], xnor_1_out[7], xnor_1_out[8], xnor_1_out[9], xnor_1_out[10], xnor_1_out[11], xnor_1_out[12], xnor_1_out[13], xnor_1_out[14], xnor_1_out[15], xnor_1_out[16], xnor_1_out[17], xnor_1_out[18], xnor_1_out[19], xnor_1_out[20], xnor_1_out[21], xnor_1_out[22], xnor_1_out[23], xnor_1_out[24], xnor_1_out[25], xnor_1_out[26], xnor_1_out[27], xnor_1_out[28], xnor_1_out[29]);
  and and_2 (and_2_out, xnor_2_out[0], xnor_2_out[1], xnor_2_out[2], xnor_2_out[3], xnor_2_out[4], xnor_2_out[5], xnor_2_out[6], xnor_2_out[7], xnor_2_out[8], xnor_2_out[9], xnor_2_out[10], xnor_2_out[11], xnor_2_out[12], xnor_2_out[13], xnor_2_out[14], xnor_2_out[15], xnor_2_out[16], xnor_2_out[17], xnor_2_out[18], xnor_2_out[19], xnor_2_out[20], xnor_2_out[21], xnor_2_out[22], xnor_2_out[23], xnor_2_out[24], xnor_2_out[25], xnor_2_out[26], xnor_2_out[27], xnor_2_out[28], xnor_2_out[29]);
  and and_3 (and_3_out, xnor_3_out[0], xnor_3_out[1], xnor_3_out[2], xnor_3_out[3], xnor_3_out[4], xnor_3_out[5], xnor_3_out[6], xnor_3_out[7], xnor_3_out[8], xnor_3_out[9], xnor_3_out[10], xnor_3_out[11], xnor_3_out[12], xnor_3_out[13], xnor_3_out[14], xnor_3_out[15], xnor_3_out[16], xnor_3_out[17], xnor_3_out[18], xnor_3_out[19], xnor_3_out[20], xnor_3_out[21], xnor_3_out[22], xnor_3_out[23], xnor_3_out[24], xnor_3_out[25], xnor_3_out[26], xnor_3_out[27], xnor_3_out[28], xnor_3_out[29]);
  and and_4 (and_4_out, xnor_4_out[0], xnor_4_out[1], xnor_4_out[2], xnor_4_out[3], xnor_4_out[4], xnor_4_out[5], xnor_4_out[6], xnor_4_out[7], xnor_4_out[8], xnor_4_out[9], xnor_4_out[10], xnor_4_out[11], xnor_4_out[12], xnor_4_out[13], xnor_4_out[14], xnor_4_out[15], xnor_4_out[16], xnor_4_out[17], xnor_4_out[18], xnor_4_out[19], xnor_4_out[20], xnor_4_out[21], xnor_4_out[22], xnor_4_out[23], xnor_4_out[24], xnor_4_out[25], xnor_4_out[26], xnor_4_out[27], xnor_4_out[28], xnor_4_out[29]);
  or or_1 (or_1_out, and_1_out, and_3_out, and_2_out, and_4_out);
  LED led_1 (.in(or_1_out));
  not not_1 (not_1_out, or_1_out);
  LED led_2 (.in(not_1_out));
  RAM #(.addrWidth(2), .dataWidth(30)) ram_5 (.addr(2'b11), .data(ram_5_data), .sel(not_1_out));  // open: clk, ld, clr
  // Probe on ram_5_data
endmodule

module my_comparator (
  input  [29:0] in_1,
  input  [29:0] in_2,
  output out_3
);

  wire [29:0] xnor_1_out;

  assign xnor_1_out = ~(in_1 ^ in_2);  // XNOR_Gate xnor_1, 30 bits wide
  and and_1 (out_3, xnor_1_out[0], xnor_1_out[1], xnor_1_out[2], xnor_1_out[3], xnor_1_out[4], xnor_1_out[5], xnor_1_out[6], xnor_1_out[7], xnor_1_out[8], xnor_1_out[9], xnor_1_out[10], xnor_1_out[11], xnor_1_out[12], xnor_1_out[13], xnor_1_out[14], xnor_1_out[15], xnor_1_out[16], xnor_1_out[17], xnor_1_out[18], xnor_1_out[19], xnor_1_out[20], xnor_1_out[21], xnor_1_out[22], xnor_1_out[23], xnor_1_out[24], xnor_1_out[25], xnor_1_out[26], xnor_1_out[27], xnor_1_out[28], xnor_1_out[29]);
endmodule
